// Logisim project Q1_F1 NAND.circ as structural Verilog: 1 circuit, main circuit main
module main (
  input  A,
  input  B,
  input  C,
  input  D,
  output out_5
);

  wire nand_1_out, nand_2_out, nand_3_out;

  nand nand_1 (nand_1_out, B, B);
  nand nand_2 (nand_2_out, D, D);
  nand nand_3 (nand_3_out, A, nand_2_out, nand_1_out);
  nand nand_4 (out_5, nand_3_out, C);

  // Notes on the sheet:
  //   (Question 1) Function 1 (NAND)
endmodule
