// Logisim project Q2_F'.circ as structural Verilog: 1 circuit, main circuit main
module main (
  input  A,
  input  B,
  input  C,
  input  D,
  output out_5
);

  wire nand_1_out, nand_2_out, nand_3_out, nand_4_out, nand_5_out, nand_6_out, nand_7_out, nand_8_out,
       nand_9_out;

  nand nand_1 (nand_1_out, A, A);
  nand nand_2 (nand_2_out, D, nand_1_out, nand_3_out);
  nand nand_3 (nand_3_out, C, C);
  nand nand_4 (nand_4_out, D, D);
  nand nand_5 (nand_5_out, nand_4_out, nand_6_out, B);
  nand nand_6 (nand_6_out, C, C);
  nand nand_7 (nand_7_out, A, A);
  nand nand_8 (nand_8_out, nand_7_out, nand_9_out, D);
  nand nand_9 (nand_9_out, B, B);
  nand nand_10 (out_5, nand_2_out, nand_5_out, nand_8_out);

  // Notes on the sheet:
  //   (Question2) F' = BC'D' + A'C'D + A'B'D
endmodule
