// Logisim project Q2_F.circ as structural Verilog: 1 circuit, main circuit main
module main (
  input  A,
  input  B,
  input  C,
  input  D,
  output out_5
);

  wire nand_1_out, nand_2_out, nand_3_out, nand_4_out, nand_5_out;

  nand nand_1 (nand_1_out, B, B);
  nand nand_2 (nand_2_out, D, D);
  nand nand_3 (nand_3_out, A, D);
  nand nand_4 (nand_4_out, B, C);
  nand nand_5 (nand_5_out, nand_1_out, nand_2_out);
  nand nand_6 (out_5, nand_3_out, nand_4_out, nand_5_out);

  // Notes on the sheet:
  //   (Question2) F = B'D' + AD + BC
endmodule
