// Logisim project Logisim.circ as structural Verilog: 1 circuit, main circuit main
module main (
  input  I5,
  input  I4,
  input  I3,
  input  I2,
  input  I1,
  input  I0,
  input  sw,
  input  ld,
  input  cl,
  output Q5,
  output Q4,
  output Q3,
  output Q2,
  output Q1,
  output Q0
);

  wire and_1_out, and_2_out, and_3_out, and_4_out, clock_1_out, multiplexer_1_out, multiplexer_2_out,
       multiplexer_3_out, multiplexer_4_out, multiplexer_5_out, multiplexer_6_out, not_1_out, not_2_out,
       not_3_out, not_4_out, not_5_out;
  wire [1:0] or_2_out;

  not not_1 (not_1_out, cl);
  not not_2 (not_2_out, ld);
  not not_3 (not_3_out, cl);
  not not_4 (not_4_out, cl);
  not not_5 (not_5_out, ld);
  and and_1 (and_1_out, not_1_out, not_2_out, sw);
  and and_2 (and_2_out, not_3_out, ld);
  and and_3 (and_3_out, not_4_out, not_5_out, sw);
  buf and_4 (and_4_out, cl);  // AND_Gate
  or or_1 (or_2_out[1], and_1_out, and_2_out);
  or or_2 (or_2_out[0], and_3_out, and_4_out);
  Clock clock_1 (.out(clock_1_out));
  Multiplexer #(.select(2)) multiplexer_1 (
    .in0(Q5), .in1(1'b0), .in2(I5), .in3(Q4), .out(multiplexer_1_out), .sel(or_2_out), .en(1'b1));
  Register #(.width(1)) register_1 (.D(multiplexer_1_out), .Q(Q5), .clk(clock_1_out));  // open: en, clr
  Multiplexer #(.select(2)) multiplexer_2 (
    .in0(Q4), .in1(1'b0), .in2(I4), .in3(Q5), .out(multiplexer_2_out), .sel(or_2_out), .en(1'b1));
  Register #(.width(1)) register_2 (.D(multiplexer_2_out), .Q(Q4), .clk(clock_1_out));  // open: en, clr
  Multiplexer #(.select(2)) multiplexer_3 (
    .in0(Q3), .in1(1'b0), .in2(I3), .in3(Q2), .out(multiplexer_3_out), .sel(or_2_out), .en(1'b1));
  Register #(.width(1)) register_3 (.D(multiplexer_3_out), .Q(Q3), .clk(clock_1_out));  // open: en, clr
  Multiplexer #(.select(2)) multiplexer_4 (
    .in0(Q2), .in1(1'b0), .in2(I2), .in3(Q3), .out(multiplexer_4_out), .sel(or_2_out), .en(1'b1));
  Register #(.width(1)) register_4 (.D(multiplexer_4_out), .Q(Q2), .clk(clock_1_out));  // open: en, clr
  Multiplexer #(.select(2)) multiplexer_5 (
    .in0(Q1), .in1(1'b0), .in2(I1), .in3(Q0), .out(multiplexer_5_out), .sel(or_2_out), .en(1'b1));
  Register #(.width(1)) register_5 (.D(multiplexer_5_out), .Q(Q1), .clk(clock_1_out));  // open: en, clr
  Multiplexer #(.select(2)) multiplexer_6 (
    .in0(Q0), .in1(1'b0), .in2(I0), .in3(Q1), .out(multiplexer_6_out), .sel(or_2_out), .en(1'b1));
  Register #(.width(1)) register_6 (.D(multiplexer_6_out), .Q(Q0), .clk(clock_1_out));  // open: en, clr

  // Notes on the sheet:
  //   s1
  //   s0
endmodule
