// Logisim project gates.circ as structural Verilog: 1 circuit, main circuit main
module main (
  input  in_1,
  input  in_2,
  input  in_3,
  input  in_4,
  input  in_5,
  input  in_6,
  input  [1:0] in_7,
  input  in_8,
  input  in_9,
  input  in_10,
  input  in_11,
  input  in_12,
  input  in_13,
  input  in_14,
  input  in_15,
  input  in_16,
  input  in_17,
  input  in_18,
  input  in_19,
  input  in_20,
  input  in_21,
  input  in_22,
  input  in_23,
  input  in_24,
  input  in_25,
  input  in_26,
  input  in_27,
  input  in_28,
  output out_29,
  output out_30,
  output out_31,
  output out_32,
  output out_33,
  output out_34,
  output out_35,
  output out_36,
  output out_37,
  output out_38,
  output out_39,
  output out_40,
  output out_41,
  output out_42
);

  wire nand_1_out, nand_3_out, nand_4_out, nand_6_out, nand_7_out, nand_8_out, nor_1_out, nor_3_out,
       nor_4_out, nor_5_out, nor_7_out, nor_8_out, nor_10_out, nor_11_out, nor_12_out, not_1_out, not_2_out,
       not_3_out, not_4_out, not_7_out, not_8_out, not_10_out, not_11_out, not_12_out, not_13_out,
       not_14_out, not_15_out, not_17_out, not_18_out, not_19_out, not_20_out;

  Multiplexer multiplexer_1 (.in0(in_1), .in1(in_3), .out(out_30), .sel(in_4), .en(in_5));
  not not_1 (not_1_out, in_11);
  not not_2 (not_2_out, in_12);
  not not_3 (not_3_out, in_15);
  not not_4 (not_4_out, in_19);
  nand nand_1 (nand_1_out, in_22, in_25);
  nor nor_1 (nor_1_out, not_1_out, not_2_out);
  not not_5 (out_34, nor_1_out);
  nor nor_2 (out_37, not_3_out, not_4_out);
  not not_6 (out_39, nand_1_out);
  Decoder #(.select(2)) decoder_1 (.out1(out_29), .out3(out_31), .sel(in_7), .en(in_6));  // open: out0, out2
  not not_7 (not_7_out, in_23);
  not not_8 (not_8_out, in_26);
  not not_9 (out_38, nor_3_out);
  nor nor_3 (nor_3_out, in_16, in_20);
  nand nand_2 (out_40, not_7_out, not_8_out);
  not not_10 (not_10_out, in_2);
  nor nor_4 (nor_4_out, not_10_out, in_8);
  nor nor_5 (nor_5_out, in_2, not_11_out);
  not not_11 (not_11_out, in_8);
  nor nor_6 (out_33, in_9, in_10);
  not not_12 (not_12_out, in_13);
  not not_13 (not_13_out, in_17);
  not not_14 (not_14_out, in_21);
  not not_15 (not_15_out, in_27);
  nor nor_7 (nor_7_out, not_12_out, in_17);
  nor nor_8 (nor_8_out, in_13, not_13_out);
  nand nand_3 (nand_3_out, not_14_out, in_27);
  nand nand_4 (nand_4_out, in_21, not_15_out);
  nor nor_9 (out_32, nor_4_out, nor_5_out);
  nor nor_10 (nor_10_out, nor_7_out, nor_8_out);
  not not_16 (out_35, nor_10_out);
  nand nand_5 (out_41, nand_3_out, nand_4_out);
  not not_17 (not_17_out, in_14);
  not not_18 (not_18_out, in_18);
  not not_19 (not_19_out, in_24);
  not not_20 (not_20_out, in_28);
  nor nor_11 (nor_11_out, not_17_out, in_18);
  nor nor_12 (nor_12_out, in_14, not_18_out);
  nand nand_6 (nand_6_out, not_19_out, in_28);
  nand nand_7 (nand_7_out, in_24, not_20_out);
  nor nor_13 (out_36, nor_11_out, nor_12_out);
  nand nand_8 (nand_8_out, nand_6_out, nand_7_out);
  not not_21 (out_42, nand_8_out);

  // Notes on the sheet:
  //   NAND Gate
  //   AND Gate
  //   AND Gate
  //   OR Gate
  //   OR Gate
  //   XNOR Gate
  //   XOR Gate
  //   XOR Gate
  //   XNOR Gate
  //   XNOR Gate
endmodule
